# Fritzing sketch raPID_FC (saved by Fritzing 0.9.3b)
circuit board: 7.29735cm x 5.39684cm
breadboards: 1

parts:
  Teensy_3_2 = Teensy 3.1
  RCIN = Header 12 [package=1x12_machine-pin-header_lock.004]
  VIN = Header 2 [package=molex-1x2_lock]
  Servo_driver = 16-Channel 12-bit PWM Servo Driver - I2C [part_number=815]
  MPU6050 = MPU-6050 Board GY-521 [form="♀ (female)" package=THT]
  S1 = Round Pushbutton
  R1 = Rotary Potentiometer (Large) [maximum_resistance=100kΩ package=THT]
  R2 = Resistor [tolerance=±5% resistance=220 package=THT]
  S2 = Toggle Switch [package=THT]
  S3 = Toggle Switch [package=THT]
  LED = LED - 3mm [color="Red (633nm)" package="3 mm [THT]"]
  DAC = LED - 3mm [color="Red (633nm)" package="3 mm [THT]"]
  DBG = LED - 3mm [color="Red (633nm)" package="3 mm [THT]"]

nets:
  GND: Teensy_3_2.GND, VIN.1, Servo_driver.GND, MPU6050.pin2, S1.leg1, R1.leg2, LED.anode, DAC.anode
  N1: Teensy_3_2.D0, RCIN.1
  N2: Teensy_3_2.D1, RCIN.2
  N3: Teensy_3_2.D2, RCIN.3
  N4: Teensy_3_2.D3, RCIN.4
  N5: Teensy_3_2.D4, RCIN.5
  N6: Teensy_3_2.D5, RCIN.6
  N7: Teensy_3_2.D6, RCIN.7
  N8: Teensy_3_2.D7, RCIN.8
  N9: Teensy_3_2.D8, RCIN.9
  N10: Teensy_3_2.D9, RCIN.10
  N11: Teensy_3_2.D10, RCIN.11
  N12: Teensy_3_2.D11, RCIN.12
  N13: Teensy_3_2.D12, MPU6050.pin8
  N14: Teensy_3_2.A14/DAC, MPU6050.pin5, DAC.cathode
  N15: Teensy_3_2.D13, S1.leg0
  N16: Teensy_3_2.A0/D14, S3.L2
  N17: Teensy_3_2.A1/D15, R1.wiper
  N18: Teensy_3_2.A2/D16, S3.COM
  N19: Teensy_3_2.A3/D17, S3.L1
  N20: Teensy_3_2.A4/D18, Servo_driver.SDA, MPU6050.pin4
  N21: Teensy_3_2.A5/D19, Servo_driver.SCL, MPU6050.pin3
  N22: Teensy_3_2.A6/D20, S2.L2
  N23: Teensy_3_2.A7/D21, S2.COM
  N24: Teensy_3_2.A8/D22, S2.L1, DBG.cathode
  N25: Teensy_3_2.A9/D23, R2.Pin_1, DBG.anode
  N26: Teensy_3_2.3V3, MPU6050.pin1, R1.leg1
  VIN: Teensy_3_2.Vin, VIN.2, Servo_driver.VCC
  N27: R2.Pin_0, LED.cathode

custom parts:
  16-Channel 12-bit PWM Servo Driver - I2C: You want to make a cool robot, maybe a hexapod walker, or maybe just a piece of art with a lot of moving parts. Or maybe you want to drive a lot of LEDs with precise PWM output. Using only two pins, control 16 free-running PWM outputs! You can even chain up 62 breakouts to control up to 992 PWM outputs.
  MPU-6050 Board GY-521: Acelerometro y Giroscopio MPU-6050 Board GY-521
