# Fritzing sketch raPID_FC_mini (saved by Fritzing 0.9.3b)
circuit board: 4.75345cm x 2.87543cm
breadboards: 1

parts:
  VIN1 = female pin header, 2 pins [form="♀ (female)"]
  RX1 = female pin header, 2 pins [form="♀ (female)"]
  J7 = female pin header, 4 pins [form="♀ (female)"]
  J8 = female pin header, 4 pins [form="♀ (female)"]
  J9 = female pin header, 4 pins [form="♀ (female)"]
  1_2_3_4_5_7 = female pin header, 6 pins [form="♀ (female)"]
  J11 = female pin header, 2 pins [form="♀ (female)"]
  J12 = female pin header, 1 pin [form="♀ (female)"]
  J13 = female pin header, 1 pin [form="♀ (female)"]
  J14 = female pin header, 1 pin [form="♀ (female)"]
  J15 = female pin header, 1 pin [form="♀ (female)"]
  J16 = female pin header, 4 pins [form="♀ (female)"]
  J17 = female pin header, 6 pins [form="♀ (female)"]
  J18 = female pin header, 1 pin [form="♀ (female)"]
  J19 = female pin header, 4 pins [form="♀ (female)"]
  a_b_c_d = female pin header, 4 pins [form="♀ (female)"]
  J10 = female pin header, 4 pins [form="♀ (female)"]
  e_f_g_h = female pin header, 4 pins [form="♀ (female)"]
  J20 = female pin header, 4 pins [form="♀ (female)"]
  J21 = female pin header, 1 pin [form="♀ (female)"]

nets:
  N1: VIN1.pin1, RX1.pin2, J9.pin1, J9.pin2, J9.pin3, J9.pin4, J15.pin1
  N2: VIN1.pin2, RX1.pin1, J14.pin1
  N3: J7.pin1, J16.pin1
  N4: J7.pin2, J16.pin2
  N5: J7.pin3, J16.pin3
  N6: J7.pin4, J16.pin4
  N7: J8.pin1, J8.pin2, J8.pin3, J8.pin4, J13.pin1, J20.pin1
  N8: 1_2_3_4_5_7.pin1, J17.pin1
  N9: 1_2_3_4_5_7.pin2, J17.pin2
  N10: 1_2_3_4_5_7.pin3, J17.pin3
  N11: 1_2_3_4_5_7.pin4, J17.pin4
  N12: 1_2_3_4_5_7.pin5, J17.pin5
  N13: 1_2_3_4_5_7.pin6, J17.pin6
  N14: J11.pin1, J20.pin4
  N15: J11.pin2, J20.pin3
  N16: J12.pin1, J20.pin2
  N17: J18.pin1, J21.pin1
  N18: J19.pin1, a_b_c_d.pin1
  N19: J19.pin2, a_b_c_d.pin2
  N20: J19.pin3, a_b_c_d.pin3
  N21: J19.pin4, a_b_c_d.pin4
  N22: J10.pin1, e_f_g_h.pin1
  N23: J10.pin2, e_f_g_h.pin2
  N24: J10.pin3, e_f_g_h.pin3
  N25: J10.pin4, e_f_g_h.pin4
